// Logisim project decoder_circuit.circ as structural Verilog: 1 circuit, main circuit main
module main (
  input  En,
  input  A,
  input  B,
  input  C,
  output o0,
  output o1,
  output o2,
  output o3,
  output o4,
  output o5,
  output o6,
  output o7
);

  wire not_1_out, not_2_out, not_3_out;

  not not_1 (not_1_out, A);
  not not_2 (not_2_out, B);
  not not_3 (not_3_out, C);
  and and_1 (o0, not_1_out, not_2_out, not_3_out, En);
  and and_2 (o1, not_1_out, not_2_out, C, En);
  and and_3 (o2, not_1_out, B, not_3_out, En);
  and and_4 (o3, not_1_out, B, C, En);
  and and_5 (o4, A, not_2_out, not_3_out, En);
  and and_6 (o5, A, not_2_out, C, En);
  and and_7 (o6, A, B, not_3_out, En);
  and and_8 (o7, A, B, C, En);

  // Notes on the sheet:
  //   3x8 Decoder
endmodule
